// Logisim project MEUPS.circ as structural Verilog: 5 circuits, main circuit main
module main (
  input  in_1
);

  wire and_1_out, button_1_out, Clear, CLK, clock_1_out, meuc_1_branch, meuc_1_jump, meuc_1_memread,
       meuc_1_memtoreg, meuc_1_memwrite, meuc_1_regn, meuc_1_regwrite, meuc_1_ulaval, not_1_out, or_2_out,
       ula_1_zero;
  wire [3:0] meuc_1_ulacode, multiplexer_1_out;
  wire [15:0] adder_1_out, adder_2_out, bit_extender_2_out, multiplexer_3_out, register_1_q;
  wire [31:0] banco_de_registradores_1_r0_2, banco_de_registradores_1_r1_2, bit_extender_1_out,
       multiplexer_2_out, multiplexer_4_out, ram_1_data, ram_2_data, ula_1_resultado;

  or or_1 (CLK, clock_1_out, button_1_out);
  Clock clock_1 (.out(clock_1_out));
  Button button_1 (.out(button_1_out));
  Register #(.width(16), .Select("low")) register_1 (
    .D(multiplexer_3_out), .en(in_1), .Q(register_1_q), .clk(CLK), .clr(Clear));
  Button button_2 (.out(Clear));
  Adder #(.width(16)) adder_1 (.a(16'h1), .b(register_1_q), .out(adder_1_out));  // open: cin, cout
  RAM #(.addrWidth(16), .dataWidth(32), .Select("low")) ram_1 (
    .addr(register_1_q), .data(ram_1_data));  // open: sel, clk, ld, clr
  UC uc_1 ();  // open: OPCOD, RegDST, Jump, Branch, MemRead, MemToReg, ULAOP, MemWrite, ULAVAL, RegWrite
  MEUC meuc_1 (
    .A(ram_1_data[31:28]), .RegN(meuc_1_regn), .Jump(meuc_1_jump), .Branch(meuc_1_branch),
    .MemRead(meuc_1_memread), .MemToReg(meuc_1_memtoreg), .MemWrite(meuc_1_memwrite), .ULAVAL(meuc_1_ulaval),
    .RegWrite(meuc_1_regwrite), .ULACODE(meuc_1_ulacode));
  Multiplexer #(.width(4), .enable("false")) multiplexer_1 (
    .in0(ram_1_data[19:16]), .in1(ram_1_data[27:24]), .out(multiplexer_1_out), .sel(meuc_1_regn));
  Adder #(.width(16)) adder_2 (.a(adder_1_out), .b(ram_1_data[15:0]), .out(adder_2_out));  // open: cin, cout
  Banco_de_Registradores banco_de_registradores_1 (
    .RD(multiplexer_1_out), .RW(multiplexer_4_out), .Clock(CLK), .Clear(Clear),
    .R0_2(banco_de_registradores_1_r0_2), .R0(ram_1_data[27:24]), .R1_2(banco_de_registradores_1_r1_2),
    .R1(ram_1_data[23:20]), .RW_Select(meuc_1_regwrite));
  assign bit_extender_1_out = {{16{1'b0}}, ram_1_data[15:0]};  // Bit_Extender bit_extender_1
  ULA ula_1 (
    .R0(banco_de_registradores_1_r0_2), .R1(multiplexer_2_out), .Zero(ula_1_zero),
    .\Operação (meuc_1_ulacode), .Resultado(ula_1_resultado));
  Multiplexer #(.width(32), .enable("false")) multiplexer_2 (
    .in0(banco_de_registradores_1_r1_2), .in1(bit_extender_1_out), .out(multiplexer_2_out),
    .sel(meuc_1_ulaval));
  Multiplexer #(.width(16), .enable("false")) multiplexer_3 (
    .in0(adder_1_out), .in1(adder_2_out), .out(multiplexer_3_out), .sel(or_2_out));
  or or_2 (or_2_out, and_1_out, meuc_1_jump);
  and and_1 (and_1_out, meuc_1_branch, ula_1_zero);
  Bit_Extender #(.in_width(32), .\type ("zero")) bit_extender_2 (.in(ula_1_resultado), .out(bit_extender_2_out));
  not not_1 (not_1_out, CLK);
  RAM #(.addrWidth(16), .dataWidth(32), .bus("separate"), .Select("high")) ram_2 (
    .addr(bit_extender_2_out), .din(banco_de_registradores_1_r1_2), .data(ram_2_data), .str(meuc_1_memwrite),
    .sel(in_1), .clk(not_1_out), .ld(meuc_1_memread), .clr(Clear));
  Multiplexer #(.width(32), .enable("false")) multiplexer_4 (
    .in0(ram_2_data), .in1(ula_1_resultado), .out(multiplexer_4_out), .sel(meuc_1_memtoreg));

  // Other names for the same wires on the sheet: ON = in_1
endmodule

module Banco_de_Registradores (
  input  RW_Select,
  input  [3:0] RD,
  input  [31:0] RW,
  input  Clock,
  input  Clear,
  input  [3:0] R0,
  input  [3:0] R1,
  output [31:0] R0_2,
  output [31:0] R1_2
);

  wire demultiplexer_1_out0, demultiplexer_1_out1, demultiplexer_1_out2, demultiplexer_1_out3,
       demultiplexer_1_out4, demultiplexer_1_out5, demultiplexer_1_out6, demultiplexer_1_out7,
       demultiplexer_1_out8, demultiplexer_1_out9, demultiplexer_1_out10, demultiplexer_1_out11,
       demultiplexer_1_out12, demultiplexer_1_out13, demultiplexer_1_out14, demultiplexer_1_out15;
  wire [31:0] register_1_q, register_2_q, register_3_q, register_4_q, register_5_q, register_6_q,
       register_7_q, register_8_q, register_9_q, register_10_q, register_11_q, register_12_q, register_13_q,
       register_14_q, register_15_q, register_16_q;

  Register #(.width(32), .Select("low")) register_1 (
    .D(RW), .en(demultiplexer_1_out0), .Q(register_1_q), .clk(Clock), .clr(Clear));
  Register #(.width(32), .Select("low")) register_2 (
    .D(RW), .en(demultiplexer_1_out1), .Q(register_2_q), .clk(Clock), .clr(Clear));
  Register #(.width(32), .Select("low")) register_3 (
    .D(RW), .en(demultiplexer_1_out2), .Q(register_3_q), .clk(Clock), .clr(Clear));
  Register #(.width(32), .Select("low")) register_4 (
    .D(RW), .en(demultiplexer_1_out3), .Q(register_4_q), .clk(Clock), .clr(Clear));
  Register #(.width(32), .Select("low")) register_5 (
    .D(RW), .en(demultiplexer_1_out4), .Q(register_5_q), .clk(Clock), .clr(Clear));
  Register #(.width(32), .Select("low")) register_6 (
    .D(RW), .en(demultiplexer_1_out5), .Q(register_6_q), .clk(Clock), .clr(Clear));
  Register #(.width(32), .Select("low")) register_7 (
    .D(RW), .en(demultiplexer_1_out6), .Q(register_7_q), .clk(Clock), .clr(Clear));
  Register #(.width(32), .Select("low")) register_8 (
    .D(RW), .en(demultiplexer_1_out7), .Q(register_8_q), .clk(Clock), .clr(Clear));
  Demultiplexer #(.select(4), .enable("false")) demultiplexer_1 (
    .out0(demultiplexer_1_out0), .out1(demultiplexer_1_out1), .out2(demultiplexer_1_out2),
    .out3(demultiplexer_1_out3), .out4(demultiplexer_1_out4), .out5(demultiplexer_1_out5),
    .out6(demultiplexer_1_out6), .out7(demultiplexer_1_out7), .out8(demultiplexer_1_out8),
    .out9(demultiplexer_1_out9), .out10(demultiplexer_1_out10), .out11(demultiplexer_1_out11),
    .out12(demultiplexer_1_out12), .out13(demultiplexer_1_out13), .out14(demultiplexer_1_out14),
    .out15(demultiplexer_1_out15), .in(RW_Select), .sel(RD));
  Register #(.width(32), .Select("low")) register_9 (
    .D(RW), .en(demultiplexer_1_out8), .Q(register_9_q), .clk(Clock), .clr(Clear));
  Register #(.width(32), .Select("low")) register_10 (
    .D(RW), .en(demultiplexer_1_out9), .Q(register_10_q), .clk(Clock), .clr(Clear));
  Register #(.width(32), .Select("low")) register_11 (
    .D(RW), .en(demultiplexer_1_out10), .Q(register_11_q), .clk(Clock), .clr(Clear));
  Register #(.width(32), .Select("low")) register_12 (
    .D(RW), .en(demultiplexer_1_out11), .Q(register_12_q), .clk(Clock), .clr(Clear));
  Register #(.width(32), .Select("low")) register_13 (
    .D(RW), .en(demultiplexer_1_out12), .Q(register_13_q), .clk(Clock), .clr(Clear));
  Register #(.width(32), .Select("low")) register_14 (
    .D(RW), .en(demultiplexer_1_out13), .Q(register_14_q), .clk(Clock), .clr(Clear));
  Register #(.width(32), .Select("low")) register_15 (
    .D(RW), .en(demultiplexer_1_out14), .Q(register_15_q), .clk(Clock), .clr(Clear));
  Register #(.width(32), .Select("low")) register_16 (
    .D(RW), .en(demultiplexer_1_out15), .Q(register_16_q), .clk(Clock), .clr(Clear));
  Multiplexer #(.select(4), .width(32), .enable("false")) multiplexer_1 (
    .in0(register_1_q), .in1(register_2_q), .in2(register_3_q), .in3(register_4_q), .in4(register_5_q),
    .in5(register_6_q), .in6(register_7_q), .in7(register_8_q), .in8(register_9_q), .in9(register_10_q),
    .in10(register_11_q), .in11(register_12_q), .in12(register_13_q), .in13(register_14_q),
    .in14(register_15_q), .in15(register_16_q), .out(R0_2), .sel(R0));
  Multiplexer #(.select(4), .width(32), .enable("false")) multiplexer_2 (
    .in0(register_1_q), .in1(register_2_q), .in2(register_3_q), .in3(register_4_q), .in4(register_5_q),
    .in5(register_6_q), .in6(register_7_q), .in7(register_8_q), .in8(register_9_q), .in9(register_10_q),
    .in10(register_11_q), .in11(register_12_q), .in12(register_13_q), .in13(register_14_q),
    .in14(register_15_q), .in15(register_16_q), .out(R1_2), .sel(R1));

  // Other names for the same wires on the sheet: C = Clear; K = Clock
endmodule

module ULA (
  input  [31:0] R0,
  input  [31:0] R1,
  input  [3:0] \Operação ,
  output [31:0] Resultado,
  output Zero
);

  wire [31:0] adder_1_out, bit_extender_1_out, divider_1_out, multiplier_1_out, subtractor_1_out;

  Adder #(.width(32)) adder_1 (.a(R0), .b(R1), .out(adder_1_out));  // open: cin, cout
  Subtractor #(.width(32)) subtractor_1 (.a(R0), .b(R1), .out(subtractor_1_out));  // open: bin, bout
  Multiplier #(.width(32)) multiplier_1 (.a(R0), .b(R1), .out(multiplier_1_out));  // open: cin, cout
  Divider #(.width(32)) divider_1 (.a(R0), .b(R1), .out(divider_1_out));  // open: upper, rem
  Comparator #(.width(32)) comparator_1 (.a(R0), .b(R1), .eq(Zero));  // open: gt, lt
  assign bit_extender_1_out = {{31{1'b0}}, Zero};  // Bit_Extender bit_extender_1
  Multiplexer #(.select(4), .width(32), .enable("false")) multiplexer_1 (
    .in0(adder_1_out), .in1(subtractor_1_out), .in2(multiplier_1_out), .in3(divider_1_out), .out(Resultado),
    .sel(\Operação ));  // open: in4, in5, in6, in7, in8, in9, in10, in11, in12, in13, in14, in15
endmodule

module UC (
  input  [3:0] OPCOD,
  output RegDST,
  output Jump,
  output Branch,
  output MemRead,
  output MemToReg,
  output [3:0] ULAOP,
  output MemWrite,
  output ULAVAL,
  output RegWrite
);

  wire and_2_out, and_3_out, and_4_out;

  // AND_Gate and_1 is placed but not wired
  and and_2 (and_2_out, ~OPCOD[0], OPCOD[1], ~OPCOD[2], ~OPCOD[3]);  // AND_Gate
  and and_3 (and_3_out, ~OPCOD[0], ~OPCOD[1], OPCOD[2], ~OPCOD[3]);  // AND_Gate
  and and_4 (and_4_out, ~OPCOD[0], ~OPCOD[1], ~OPCOD[2], OPCOD[3]);  // AND_Gate
  buf or_1 (RegDST, 1'b0);  // OR_Gate
  buf or_2 (Jump, 1'b0);  // OR_Gate
  buf or_3 (Branch, 1'b0);  // OR_Gate
  or or_4 (MemRead, 1'b0, and_2_out);
  or or_5 (MemToReg, 1'b0, and_4_out);
  or or_6 (MemWrite, 1'b0, and_3_out);
  or or_7 (ULAVAL, 1'b0, and_3_out, and_4_out);
  or or_8 (RegWrite, 1'b0, and_2_out, and_4_out);

  assign ULAOP = 4'b0000;
endmodule

module MEUC (
  input  [3:0] A,
  output RegN,
  output Jump,
  output Branch,
  output MemRead,
  output MemToReg,
  output MemWrite,
  output ULAVAL,
  output RegWrite,
  output [3:0] ULACODE
);

  wire and_1_out, and_2_out, and_6_out, and_7_out, and_8_out, and_9_out, and_10_out, and_11_out, and_13_out,
       and_14_out, and_15_out, and_16_out, and_17_out, and_18_out, and_19_out, and_20_out, and_21_out,
       not_1_out, not_2_out, not_3_out, not_4_out, not_5_out, not_6_out, not_7_out, not_8_out, not_9_out,
       not_10_out, not_11_out, not_12_out, not_13_out, not_14_out, not_15_out, not_16_out, not_17_out,
       not_18_out, not_19_out, not_20_out, not_21_out, not_22_out, not_23_out, not_24_out, not_25_out,
       not_26_out, not_27_out, not_28_out, not_29_out;

  not not_1 (not_1_out, A[3]);
  not not_2 (not_2_out, A[1]);
  not not_3 (not_3_out, A[0]);
  not not_4 (not_4_out, A[2]);
  not not_5 (not_5_out, A[1]);
  not not_6 (not_6_out, A[0]);
  not not_7 (not_7_out, A[3]);
  not not_8 (not_8_out, A[2]);
  not not_9 (not_9_out, A[0]);
  not not_10 (not_10_out, A[3]);
  not not_11 (not_11_out, A[1]);
  not not_12 (not_12_out, A[1]);
  not not_13 (not_13_out, A[0]);
  not not_14 (not_14_out, A[0]);
  not not_15 (not_15_out, A[3]);
  not not_16 (not_16_out, A[2]);
  not not_17 (not_17_out, A[1]);
  not not_18 (not_18_out, A[3]);
  not not_19 (not_19_out, A[2]);
  not not_20 (not_20_out, A[1]);
  not not_21 (not_21_out, A[3]);
  not not_22 (not_22_out, A[0]);
  not not_23 (not_23_out, A[3]);
  not not_24 (not_24_out, A[0]);
  not not_25 (not_25_out, A[1]);
  not not_26 (not_26_out, A[0]);
  not not_27 (not_27_out, A[2]);
  not not_28 (not_28_out, A[1]);
  not not_29 (not_29_out, A[0]);
  and and_1 (and_1_out, A[3], A[1], A[0]);
  and and_2 (and_2_out, A[3], A[2], A[0]);
  and and_3 (RegN, not_1_out, A[2], not_2_out, not_3_out);
  and and_4 (Jump, A[3], not_4_out, not_5_out, A[0]);
  and and_5 (Branch, A[3], A[1], not_6_out);
  and and_6 (and_6_out, not_7_out, not_8_out, A[1], not_9_out);
  and and_7 (and_7_out, not_10_out, A[2], not_11_out, A[0]);
  and and_8 (and_8_out, not_12_out, not_13_out);
  and and_9 (and_9_out, A[1], A[0]);
  and and_10 (and_10_out, A[2], not_14_out);
  and and_11 (and_11_out, A[3], A[2]);
  and and_12 (MemWrite, not_15_out, not_16_out, not_17_out, A[0]);
  and and_13 (and_13_out, not_18_out, not_19_out, not_20_out);
  and and_14 (and_14_out, not_21_out, not_22_out);
  and and_15 (and_15_out, A[2], A[1]);
  and and_16 (and_16_out, not_23_out, not_24_out);
  and and_17 (and_17_out, not_25_out, not_26_out);
  and and_18 (and_18_out, A[1], A[0]);
  and and_19 (and_19_out, A[2], A[1], A[0]);
  and and_20 (and_20_out, A[3], not_27_out, not_28_out, not_29_out);
  and and_21 (and_21_out, A[3], A[2], A[0]);
  or or_1 (ULACODE[0], and_1_out, and_2_out);
  or or_2 (MemRead, and_6_out, and_7_out);
  or or_3 (MemToReg, and_8_out, and_9_out, and_10_out, and_11_out);
  or or_4 (ULAVAL, and_13_out, and_14_out, and_15_out);
  or or_5 (RegWrite, and_16_out, and_17_out, and_18_out, A[2]);
  or or_6 (ULACODE[1], and_19_out, and_20_out, and_21_out);

  assign ULACODE[3:2] = 2'b00;
endmodule
